// Logisim project ALU.circ as structural Verilog: 2 circuits, main circuit main
module main (
  input  [31:0] A,
  input  [4:0] in_2,
  input  [31:0] B,
  output [31:0] OUT,
  output [31:0] Hi,
  output [31:0] Lo
);

  wire BorrowRest, CoutAdd;
  wire [31:0] A0_Add, A1_Subs, A2_Mulu, A3_Mult, Add, B0_Add, B1_Subs, B2_Mulu, B3_Mult,
       demultiplexer_1_out4, demultiplexer_2_out4, Hi_Mulu, Lo_Mulu, Mult, Subs;

  // Probe on A
  // Probe on B
  Demultiplexer #(.select(5), .width(32), .enable("false")) demultiplexer_1 (
    .out0(A0_Add), .out1(A1_Subs), .out2(A2_Mulu), .out3(A3_Mult), .out4(demultiplexer_1_out4), .in(A),
    .sel(in_2));  // open: out5, out6, out7, out8, out9, out10, out11, out12, out13, out14, out15, out16, out17, out18, out19, out20, out21, out22, out23, out24, out25, out26, out27, out28, out29, out30, out31
  Demultiplexer #(.select(5), .width(32), .enable("false")) demultiplexer_2 (
    .out0(B0_Add), .out1(B1_Subs), .out2(B2_Mulu), .out3(B3_Mult), .out4(demultiplexer_2_out4), .in(B),
    .sel(in_2));  // open: out5, out6, out7, out8, out9, out10, out11, out12, out13, out14, out15, out16, out17, out18, out19, out20, out21, out22, out23, out24, out25, out26, out27, out28, out29, out30, out31
  Adder #(.width(32)) adder_1 (.a(A0_Add), .b(B0_Add), .out(Add), .cout(CoutAdd));  // open: cin
  Subtractor #(.width(32)) subtractor_1 (.a(A1_Subs), .b(B1_Subs), .out(Subs), .bout(BorrowRest));  // open: bin
  Multiplier #(.width(32)) multiplier_1 (.a(A2_Mulu), .b(B2_Mulu), .out(Hi_Mulu), .cout(Lo_Mulu));  // open: cin
  Multiplexer #(.select(5), .width(32), .enable("false")) multiplexer_1 (
    .in0(Add), .in1(Subs), .in2(Mult), .out(OUT), .sel(in_2));  // open: in3, in4, in5, in6, in7, in8, in9, in10, in11, in12, in13, in14, in15, in16, in17, in18, in19, in20, in21, in22, in23, in24, in25, in26, in27, in28, in29, in30, in31

  // Other names for the same wires on the sheet: Selector[4:0] = in_2
endmodule

module SingnedOperations (
  input  [31:0] A,
  input  [31:0] B,
  output [31:0] Hi,
  output [31:0] Lo,
  output [31:0] Lo_2
);

  // Probe on B
  Negator #(.width(32)) negator_1 (.in(B), .out(Lo));
  Negator #(.width(32)) negator_2 (.in(Lo), .out(Lo_2));
  // Probe on Lo_2
  // Probe on Lo

  // Notes on the sheet:
  //   Signed
endmodule
