// Logisim project Control Unit.circ as structural Verilog
module Contador_de_Ciclos (
  input  [3:0] Read_Time,
  input  [3:0] Write_Time,
  input  Reloj,
  input  R_W,
  input  Reset,
  output Leido,
  output Escrito
);

  wire comparator_1_eq;
  wire [3:0] multiplexer_1_out, Registro_Contador_q, Time;

  Counter #(.width(4), .max('hf)) Registro_Contador (
    .Q(Registro_Contador_q), .clk(Reloj), .clr(Reset));  // open: load, D, count, carry
  Multiplexer #(.width(4), .enable("false")) multiplexer_1 (
    .in0(Read_Time), .in1(Write_Time), .out(multiplexer_1_out), .sel(R_W));
  Comparator #(.width(4), .mode("unsigned")) comparator_1 (
    .a(Registro_Contador_q), .b(Time), .eq(comparator_1_eq));  // open: gt, lt
  Demultiplexer #(.enable("false")) demultiplexer_1 (.out0(Leido), .out1(Escrito), .in(comparator_1_eq), .sel(R_W));
  Adder #(.width(4)) adder_1 (.a(multiplexer_1_out), .b(4'b0001), .out(Time));  // open: cin, cout

  // Other names for the same wires on the sheet: CLK = Reloj

  // Notes on the sheet:
  //   Entradas de Tiempo
  //   Contador de Ciclos del Reloj
endmodule

// esperar actualizacion PC
module Control_Unit (
  input  Reloj,
  input  Reset,
  input  [3:0] operacion,
  input  HALT,
  input  Wait,
  input  in_6,
  output Load_Register_File,
  output Escribir_RAM,
  output RAM_Control,
  output STOP,
  output KBD_ENABLE,
  output Load_Program_Counter,
  output LoadMemory,
  output LOADSP,
  output TTY_ENABLE
);

  wire ALU_Tip_R_and_Tip_I, and_1_out, Camb_Instr, cambio_de_linea_q, d_ff_1_q, d_ff_2_q, d_ff_6_q, d_ff_9_q,
       demultiplexer_1_out0, demultiplexer_2_out0, demultiplexer_2_out1, demultiplexer_4_out0,
       demultiplexer_5_out0, demultiplexer_6_out0, demultiplexer_6_out1, demultiplexer_7_out0,
       demultiplexer_7_out1, EN_RND, END, guardar_adress_q, Halt_t, Jmp_nop_Jr, KBD, LeerNuevaLinea, Load,
       LSP1, LSP2, M1, M2, M3, M4, M5, Mov_Operation, or_1_out, or_2_out, or_5_out, or_7_out, or_8_out,
       or_9_out, or_10_out, Pop, R_W_RF2, Rst, Store;

  D_Flip_Flop d_ff_1 (.clk(Reloj), .D(demultiplexer_1_out0), .Q(d_ff_1_q), .preset(Reset));  // open: Qn, en, reset
  or or_1 (or_1_out, d_ff_1_q, END);
  Demultiplexer #(.enable("false")) demultiplexer_1 (
    .out0(demultiplexer_1_out0), .out1(Rst), .in(or_1_out), .sel(and_1_out));
  and and_1 (and_1_out, ~END, ~Reset);  // AND_Gate
  D_Flip_Flop Insruction_Read (.clk(Reloj), .D(or_2_out), .Q(M5), .reset(Reset));  // open: Qn, preset, en
  or or_2 (or_2_out, Rst, LeerNuevaLinea, demultiplexer_2_out0);
  or or_3 (Escribir_RAM, M2, M4);
  or or_4 (Load_Register_File, ALU_Tip_R_and_Tip_I, Mov_Operation, R_W_RF2, EN_RND, KBD);
  Demultiplexer #(.enable("false")) demultiplexer_2 (
    .out0(demultiplexer_2_out0), .out1(demultiplexer_2_out1), .in(M5), .sel(Wait));
  or or_5 (or_5_out, demultiplexer_2_out1, Camb_Instr);
  D_Flip_Flop d_ff_2 (.clk(Reloj), .D(or_5_out), .Q(d_ff_2_q), .reset(Reset));  // open: Qn, preset, en
  Demultiplexer #(.select(4), .enable("false")) demultiplexer_3 (
    .out0(Jmp_nop_Jr), .out1(ALU_Tip_R_and_Tip_I), .out2(Mov_Operation), .out3(Halt_t), .out4(TTY_ENABLE),
    .out5(EN_RND), .out6(Pop), .out7(LSP1), .out8(Store), .out9(Load), .out10(KBD), .in(d_ff_2_q),
    .sel(operacion));  // open: out11, out12, out13, out14, out15
  or or_6 (RAM_Control, M1, M2, M3, M4, M5);
  or or_7 (or_7_out, demultiplexer_4_out0, Pop);
  D_Flip_Flop d_ff_3 (.clk(Reloj), .D(or_7_out), .Q(M3), .reset(Reset));  // open: Qn, preset, en
  or or_8 (or_8_out, demultiplexer_5_out0, Load);
  or or_9 (or_9_out, demultiplexer_6_out0, Store);
  Demultiplexer #(.enable("false")) demultiplexer_4 (.out0(demultiplexer_4_out0), .out1(LSP2), .in(M3), .sel(Wait));
  D_Flip_Flop d_ff_4 (.clk(Reloj), .D(or_8_out), .Q(M1), .reset(Reset));  // open: Qn, preset, en
  D_Flip_Flop d_ff_5 (.clk(Reloj), .D(or_9_out), .Q(M2), .reset(Reset));  // open: Qn, preset, en
  or or_10 (or_10_out, LSP1, demultiplexer_7_out0);
  D_Flip_Flop d_ff_6 (.clk(Reloj), .D(TTY_ENABLE), .Q(d_ff_6_q), .reset(Reset));  // open: Qn, preset, en
  Demultiplexer #(.enable("false")) demultiplexer_5 (.out0(demultiplexer_5_out0), .out1(R_W_RF2), .in(M1), .sel(Wait));
  Demultiplexer #(.enable("false")) demultiplexer_6 (
    .out0(demultiplexer_6_out0), .out1(demultiplexer_6_out1), .in(M2), .sel(Wait));
  D_Flip_Flop d_ff_7 (.clk(Reloj), .D(or_10_out), .Q(M4), .reset(Reset));  // open: Qn, preset, en
  D_Flip_Flop d_ff_8 (.clk(Reloj), .D(KBD), .Q(KBD_ENABLE), .reset(Reset));  // open: Qn, preset, en
  Demultiplexer #(.enable("false")) demultiplexer_7 (
    .out0(demultiplexer_7_out0), .out1(demultiplexer_7_out1), .in(M4), .sel(Wait));
  D_Flip_Flop d_ff_9 (.clk(Reloj), .D(demultiplexer_7_out1), .Q(d_ff_9_q), .reset(Reset));  // open: Qn, preset, en
  or or_11 (Load_Program_Counter, Jmp_nop_Jr, ALU_Tip_R_and_Tip_I, Mov_Operation, R_W_RF2, demultiplexer_6_out1, LSP2, d_ff_9_q, EN_RND, KBD_ENABLE, d_ff_6_q);
  or or_12 (LOADSP, LSP1, LSP2);
  D_Flip_Flop esperar_actualizacionPC (
    .clk(Reloj), .D(Load_Program_Counter), .Q(LoadMemory), .reset(Reset));  // open: Qn, preset, en
  D_Flip_Flop cambio_de_linea (.clk(Reloj), .D(in_6), .Q(cambio_de_linea_q), .reset(Reset));  // open: Qn, preset, en
  D_Flip_Flop guardar_adress (
    .clk(Reloj), .D(LoadMemory), .Q(guardar_adress_q), .reset(Reset));  // open: Qn, preset, en
  Demultiplexer #(.enable("false")) demultiplexer_8 (
    .out0(Camb_Instr), .out1(LeerNuevaLinea), .in(guardar_adress_q), .sel(cambio_de_linea_q));
  D_Flip_Flop u_END (.clk(Reloj), .D(HALT), .Q(END), .reset(Reset));  // open: Qn, preset, en

  assign STOP = HALT;

  // Other names for the same wires on the sheet: CargarNuevaLinea = in_6; CLK = Reloj; CS = RAM_Control;
  //   E_KBD = KBD_ENABLE; Load_PC = Load_Program_Counter; LoadITMemory = LoadMemory; Op[3:0] = operacion; Push = LSP1;
  //   R_W_Cach = Escribir_RAM; R_W_Cach_0 = M2; R_W_Cach_1 = M4; R_W_RF = Load_Register_File;
  //   R_W_RF0 = ALU_Tip_R_and_Tip_I; R_W_RF1 = Mov_Operation; R_W_RF6 = KBD; R_W_RF5 = EN_RND; Random = EN_RND;
  //   Resert = Reset; TTY = TTY_ENABLE; TTYEN = TTY_ENABLE

  // Notes on the sheet:
  //   cargar nueva linea
  //   Entradas
  //   Selector de Operacion
  //   INDLE
  //   Control Unit
  //   Activa si se va a escribir en la RAM
  //   Activar el load de los registros
  //   Cargar info de la RAM
  //   Activa el Ram Control
  //   Jmp, nor, Jr
  //   Alu (Tipo R and Tipo I)
  //   Mover los registros
  //   Operaciones
  //   Instrucciones de Memoria
  //   Cambio de instruccion
  //   OUTPUT DATA
endmodule
