// Logisim project InstructionDecoder.circ as structural Verilog
module InstructionDec (
  input  [31:0] Instruccion,
  input  LoadInstruction,
  input  Reset,
  input  Clock,
  output [5:0] Function,
  output [4:0] Shamt,
  output [4:0] Rd,
  output [4:0] Rt,
  output [4:0] Rs,
  output [15:0] Offset,
  output [25:0] Destino,
  output [5:0] OP_Code
);

  Register #(.width(32)) register_1 (
    .D(Instruccion), .en(LoadInstruction), .Q({OP_Code, Destino}), .clk(Clock), .clr(Reset));

  assign Function = Destino[5:0];
  assign Offset = Destino[15:0];
  assign Rd = Destino[15:11];
  assign Rs = Destino[25:21];
  assign Rt = Destino[20:16];
  assign Shamt = Destino[10:6];

  // Other names for the same wires on the sheet: Instruction[31:0] = Instruccion; Load = LoadInstruction

  // Notes on the sheet:
  //   INPUTS
  //   Instrucciones de Tipo R:
  //   OP-Code: (6-bits) , Rs (5-bits)  , Rt (5-bits) , Rd(5-bits)  , Shamt(5-bits) , Function(6-bits)  
  //   Instrucciones de Tipo I
  //   OP-Code: (6-bits) , Rs (5-bits)  , Rt (5-bits) , Imm-Constante-Offset 16-bits
  //   Instrucciones de Tipo J
  //   OP-Code: (6-bits) , addr(destino) 26-bits
  //   Divide la  Instruccion
  //   OUTPUTS
endmodule

module Analicer (
);

  InstructionDec instructiondec_1 ();  // open: Instruccion, LoadInstruction, Reset, Clock, Function, Shamt, Rd, Rt, Rs, Offset, Destino, OP_Code
endmodule

module DivideOpCode (
  input  [5:0] OP_Code,
  output Op_00_0000,
  output Op_11_1000,
  output Op_11_1111,
  output I,
  output J,
  output R
);

  wire and_1_out, and_2_out, and_4_out, and_5_out, and_6_out, and_7_out, and_8_out, and_9_out, and_10_out,
       and_11_out, and_12_out, and_13_out, and_14_out, and_15_out, and_17_out, and_18_out, and_19_out,
       and_20_out;

  and and_1 (and_1_out, ~OP_Code[0], OP_Code[1], ~OP_Code[2]);  // AND_Gate
  and and_2 (and_2_out, ~OP_Code[3], ~OP_Code[4], ~OP_Code[5]);  // AND_Gate
  and and_3 (J, and_1_out, and_2_out);
  and and_4 (and_4_out, ~OP_Code[4], ~OP_Code[5]);  // AND_Gate
  and and_5 (and_5_out, ~OP_Code[4], OP_Code[5]);  // AND_Gate
  and and_6 (and_6_out, ~OP_Code[0], ~OP_Code[2], OP_Code[3]);  // AND_Gate
  and and_7 (and_7_out, ~OP_Code[0], ~OP_Code[1], OP_Code[2]);  // AND_Gate
  and and_8 (and_8_out, OP_Code[1], OP_Code[2], ~OP_Code[3]);  // AND_Gate
  and and_9 (and_9_out, OP_Code[0], ~OP_Code[1], ~OP_Code[3]);  // AND_Gate
  and and_10 (and_10_out, OP_Code[0], OP_Code[1], ~OP_Code[2]);  // AND_Gate
  and and_11 (and_11_out, and_6_out, and_4_out);
  and and_12 (and_12_out, and_7_out, and_4_out);
  and and_13 (and_13_out, and_8_out, and_4_out);
  and and_14 (and_14_out, and_9_out, and_4_out);
  and and_15 (and_15_out, and_10_out, and_5_out);
  and and_16 (Op_11_1111, OP_Code[0], OP_Code[1], OP_Code[2], OP_Code[3], OP_Code[4], OP_Code[5]);
  and and_17 (and_17_out, ~OP_Code[0], ~OP_Code[1], ~OP_Code[2]);  // AND_Gate
  and and_18 (and_18_out, OP_Code[3], OP_Code[4], OP_Code[5]);
  and and_19 (and_19_out, ~OP_Code[0], ~OP_Code[1], ~OP_Code[2]);  // AND_Gate
  and and_20 (and_20_out, ~OP_Code[3], ~OP_Code[4], ~OP_Code[5]);  // AND_Gate
  and and_21 (Op_11_1000, and_17_out, and_18_out);
  and and_22 (Op_00_0000, and_19_out, and_20_out);
  or or_1 (I, and_11_out, and_12_out, and_13_out, and_14_out, and_15_out);
  or or_2 (R, Op_11_1111, Op_11_1000, Op_00_0000);

  // Other names for the same wires on the sheet: _00_0000 = Op_00_0000; _11_1000 = Op_11_1000; _11_1111 = Op_11_1111;
  //   B0 = OP_Code[0]; B1 = OP_Code[1]; B2 = OP_Code[2]; B3 = OP_Code[3]; B4 = OP_Code[4]; B5 = OP_Code[5]

  // Notes on the sheet:
  //   OP-Code TIPO J
  //   OP-Code TIPO I
  //   OP-Code TIPO R
endmodule
